# Fritzing sketch schema (saved by Fritzing 0.9.3b)
circuit board: 8.46667cm x 5.64444cm
breadboards: 1

parts:
  Power_plug1 = Power plug
  Raspberry_Pi_1 = Raspberry Pi 3 [part_number=RPI-3-V1.2]
  Q2 = TRANSISTOR_NPN [package=to-92-ammo]
  Q3 = TRANSISTOR_NPN [package=to-92-ammo]
  Q4 = TRANSISTOR_NPN [package=to-92-ammo]
  Q5 = TRANSISTOR_NPN [package=to-92-ammo]
  LED2 = smd LED [color="Red (633nm)" package="0603 [SMD]"]
  LED3 = smd LED [color="Yellow (592nm)" package="0603 [SMD]"]
  LED5 = smd LED [color="Blue (430nm)" package="0603 [SMD]"]
  LED6 = smd LED [color="Green (555nm)" package="0603 [SMD]"]
  D1 = Rectifier Diode [part_number=1N4001 package="Melf DO-213 AB [SMD]"]
  R3 = Resistor [tolerance=±5% resistance=220 package=THT]
  R4 = Resistor [tolerance=±5% resistance=220 package=THT]
  R5 = Resistor [tolerance=±5% resistance=220 package=THT]
  R6 = Resistor [tolerance=±5% resistance=220 package=THT]
  S8 = Pushbutton [package=THT]
  S9 = Pushbutton [package=THT]
  S10 = Pushbutton [package=THT]
  S11 = Pushbutton [package=THT]

nets:
  N1: Power_plug1.GND, LED2.cathode, LED3.cathode, LED5.cathode, LED6.cathode
  N2: Power_plug1.VCC, Q2.C, Q3.C, Q4.C, Q5.C, D1.anode, S8.leg1, S9.leg1, S10.leg1, S11.leg1
  N3: Raspberry_Pi_1.3v3, R3.Pin_1, R4.Pin_1, R5.Pin_1, R6.Pin_1
  N4: Raspberry_Pi_1.GPIO26, Q2.E
  N5: Raspberry_Pi_1.GPIO21, R6.Pin_0, S11.leg0
  N6: Raspberry_Pi_1.GPIO20, Q3.E
  N7: Raspberry_Pi_1.GPIO16, R5.Pin_0, S10.leg0
  N8: Raspberry_Pi_1.GPIO7, Q4.E
  N9: Raspberry_Pi_1.GPIO8, R3.Pin_0, S9.leg0
  N10: Raspberry_Pi_1.GPIO24, Q5.E
  N11: Raspberry_Pi_1.GPIO23, R4.Pin_0, S8.leg0
  N12: Raspberry_Pi_1.GND, D1.cathode
  N13: Q2.B, LED2.anode
  N14: Q3.B, LED3.anode
  N15: Q4.B, LED5.anode
  N16: Q5.B, LED6.anode
